# Fritzing sketch TempHumPressOLED (saved by Fritzing 0.9.3b)
circuit board: 9cm x 7cm
breadboards: 1

parts:
  Micro_controller = Arduino Nano (Rev3.0)
  OLED_I2C1 = OLED 128x64 I2C Monochrome Display
  Temperature_and_humidity_sensor = Humidity and Temperature Sensor RHT03
  Pressure_sensor = Barometric Pressure Sensor - BMP180 Breakout (GY-68)

nets:
  GND: Micro_controller.GND, OLED_I2C1.GND, Temperature_and_humidity_sensor.GND_2, Pressure_sensor.GND
  N1: Micro_controller.D2, Temperature_and_humidity_sensor.Data-signal
  N2: Micro_controller.A5, OLED_I2C1.SCK, Pressure_sensor.SCL
  N3: Micro_controller.A4, OLED_I2C1.SDA, Pressure_sensor.SDA
  3V3: Micro_controller.3V3, OLED_I2C1.VDD, Temperature_and_humidity_sensor.Vcc, Pressure_sensor.3.3

custom parts:
  Barometric Pressure Sensor - BMP180 Breakout (GY-68): This is a simple breakout board for the BMP180, a high-precision, low-power barometric pressure sensor made by Bosch Sensortec. The range of measurement is from 300hPa to 1100hPa. The sensor can be supplied with voltage ranging from 1.8V to 3.6V. Operating temperature range is -40 to +85 °C. This particular breakout board (or perhaps the configuration) is produced by Shenzhen Keep Power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
